// Logisim project CPU.circ as structural Verilog: 15 circuits, main circuit main
module main (
  input  MAIN_Power_HALT,
  input  RESET_SYSTEM,
  output [7:0] JMP,
  output [7:0] Multiply_8_Significant_Bits,
  output Sign_Bit,
  output Carry_Bit
);

  wire and_1_out, Clock_out, control_unit_1_ir_clock, control_unit_1_pc_clock, control_unit_1_rf_clock, HAlt,
       Jmp_decode, Jmp_t, Load, MAR, MUX_ALU_Select, not_1_out, not_2_out, RM_Clock, RY_Clock,
       step_counter_1_t1, step_counter_1_t2, step_counter_1_t3, step_counter_1_t4, step_counter_1_t5,
       step_counter_1_t6, step_counter_1_t7, step_counter_1_t8, Store;
  wire [1:0] instruction_register_and_decoder_1_a_address, instruction_register_and_decoder_1_b_address;
  wire [2:0] instruction_register_and_decoder_1_alu_opcode, MMU;
  wire [7:0] alu_1__0_7_bits, Jmp_Offset, MAR_q, Memory_Address, multiplexer_1_out, multiplexer_2_out,
       multiplexer_3_out, pc_1_jmp, ram_1_data, register_file_1_a_data, register_file_1_b_data, RM_in,
       transistor_2_out;

  Clock Clock (.out(Clock_out));
  PC pc_1 (
    .CC_Jump_Enable(Jmp_t), .Subroutine_Call_Address(Jmp_Offset), .Halt(HAlt), .Subroutine_Call_enable(1'b0),
    .PC_Clock(control_unit_1_pc_clock), .JMP(pc_1_jmp), .Jump_Offset(Jmp_Offset), .Reset(RESET_SYSTEM));
  Step_Counter step_counter_1 (
    .Main_Clock(Clock_out), .T8(step_counter_1_t8), .T1(step_counter_1_t1), .T2(step_counter_1_t2),
    .T3(step_counter_1_t3), .T4(step_counter_1_t4), .T5(step_counter_1_t5), .T6(step_counter_1_t6),
    .T7(step_counter_1_t7), .Main_Power_Step_counter(MAIN_Power_HALT));
  Control_Unit control_unit_1 (
    .T1(step_counter_1_t1), .T3(step_counter_1_t3), .T2(step_counter_1_t2), .T4(step_counter_1_t4),
    .T5(step_counter_1_t5), .T6(step_counter_1_t6), .T7(step_counter_1_t7), .T8(step_counter_1_t8),
    .IR_Clock(control_unit_1_ir_clock), .Memory_Select(MMU[0]), .MDR_Clock(MMU[2]), .RY(RY_Clock),
    .PC_Clock(control_unit_1_pc_clock), .Load(Load), .Jmp(Jmp_decode), .Store(Store), .RM_clock(RM_Clock),
    .MAR_clock(MAR), .RF_Clock(control_unit_1_rf_clock), .Load_2(MMU[1]), .JMP_Enable(Jmp_t));
  Multiplexer #(.width(8)) multiplexer_1 (
    .in0(pc_1_jmp), .in1(Memory_Address), .out(multiplexer_1_out), .sel(and_1_out), .en(1'b1));
  Register u_MAR (.D(multiplexer_1_out), .en(1'b1), .Q(MAR_q), .clk(MAR));  // open: clr
  not not_1 (not_1_out, MUX_ALU_Select);
  RAM #(.bus("asynch")) ram_1 (.addr(MAR_q), .data(ram_1_data), .sel(MMU[0]), .ld(MMU[1]), .clr(RESET_SYSTEM));
  Transistor #(.gate("br"), .width(8)) transistor_1 (.in(Jmp_Offset), .out(ram_1_data), .gate(MMU[1]));
  Register_File register_file_1 (
    .Reset_Registers(RESET_SYSTEM), .T2_Clock(control_unit_1_rf_clock), .C_Data(JMP),
    .A_Address(instruction_register_and_decoder_1_a_address),
    .B_Address(instruction_register_and_decoder_1_b_address), .A_Data(register_file_1_a_data),
    .B_Data(register_file_1_b_data), .C_Address(instruction_register_and_decoder_1_b_address));
  Multiplexer #(.width(8)) multiplexer_2 (
    .in0(Jmp_Offset), .in1(register_file_1_a_data), .out(multiplexer_2_out), .sel(not_1_out), .en(1'b1));
  ALU alu_1 (
    .ALU_OP_SELECT(instruction_register_and_decoder_1_alu_opcode), ._8_15_Bits(Multiply_8_Significant_Bits),
    .Carry_Bit_IN(Carry_Bit), .Sign_Bit(Sign_Bit), .Carry_Bit_IN_2(Carry_Bit), ._0_7_Bits(alu_1__0_7_bits),
    .Carry_Bit_OUT(Carry_Bit), .RB(register_file_1_b_data), .RA(multiplexer_2_out));
  Transistor #(.gate("br"), .width(8)) transistor_2 (.in(ram_1_data), .out(transistor_2_out), .gate(not_2_out));
  Transistor #(.width(8)) transistor_3 (.in(RM_in), .out(transistor_2_out), .gate(MMU[1]));
  not not_2 (not_2_out, MMU[1]);
  Instruction_Register_And_Decoder instruction_register_and_decoder_1 (
    .MDR_to_IR_Data(Jmp_Offset), .IR_Clock(control_unit_1_ir_clock), .Reset_IR(RESET_SYSTEM),
    .B_Address(instruction_register_and_decoder_1_b_address),
    .A_Address(instruction_register_and_decoder_1_a_address), .Load_Enable(Load), .Store_Enable(Store),
    .Jump_Enable(Jmp_decode), .Halt_Enable(HAlt), .ALU_Opcode(instruction_register_and_decoder_1_alu_opcode));  // open: Mul_Enable, Sub_Enable, Add_Enable, And_Enable, Or_Enable, XOR_Enable, Move_Enable, No_Operation_decoded_CSig_MDR
  Register RY (.D(alu_1__0_7_bits), .en(1'b1), .Q(Memory_Address), .clk(RY_Clock), .clr(RESET_SYSTEM));
  Multiplexer #(.width(8)) multiplexer_3 (
    .in0(Memory_Address), .in1(Jmp_Offset), .out(multiplexer_3_out), .sel(Load), .en(1'b1));
  Transistor #(.gate("br"), .width(8)) transistor_4 (.in(multiplexer_3_out), .out(JMP), .gate(Store));
  Register MDR (.D(transistor_2_out), .en(1'b1), .Q(Jmp_Offset), .clk(MMU[2]), .clr(RESET_SYSTEM));
  or or_1 (MUX_ALU_Select, Load, Store);
  Register RM (.D(register_file_1_a_data), .en(1'b1), .Q(RM_in), .clk(RM_Clock), .clr(RESET_SYSTEM));
  and and_1 (and_1_out, step_counter_1_t6, MUX_ALU_Select);

  // Other names for the same wires on the sheet: MDR_IR[7:0] = Jmp_Offset; MUX_MDR_ALU[7:0] = Jmp_Offset;
  //   RC[7:0] = JMP; Reset = RESET_SYSTEM
endmodule

module Register_File (
  input  Reset_Registers,
  input  T2_Clock,
  input  [1:0] A_Address,
  input  [1:0] B_Address,
  input  [7:0] C_Data,
  input  [1:0] C_Address,
  output [7:0] A_Data,
  output [7:0] B_Data
);

  wire and_1_out, and_2_out, and_3_out, and_4_out, not_1_out, not_2_out, not_3_out, not_4_out, not_5_out,
       not_6_out;
  wire [7:0] demultiplexer_1_out0, demultiplexer_1_out1, demultiplexer_1_out2, demultiplexer_1_out3, R1_q,
       R2_q, R3_q, R4_q, transistor_1_out, transistor_2_out, transistor_3_out, transistor_4_out;

  not not_1 (not_1_out, and_2_out);
  not not_2 (not_2_out, and_1_out);
  and and_1 (and_1_out, C_Address[1], not_6_out);
  and and_2 (and_2_out, C_Address[1], C_Address[0]);
  not not_3 (not_3_out, C_Address[1]);
  not not_4 (not_4_out, and_3_out);
  not not_5 (not_5_out, and_4_out);
  and and_3 (and_3_out, not_3_out, C_Address[0]);
  and and_4 (and_4_out, not_3_out, not_6_out);
  not not_6 (not_6_out, C_Address[0]);
  Demultiplexer #(.select(2), .width(8)) demultiplexer_1 (
    .out0(demultiplexer_1_out0), .out1(demultiplexer_1_out1), .out2(demultiplexer_1_out2),
    .out3(demultiplexer_1_out3), .in(C_Data), .sel(C_Address), .en(1'b1));
  Transistor #(.gate("br"), .width(8)) transistor_1 (
    .in(demultiplexer_1_out3), .out(transistor_1_out), .gate(not_1_out));
  Transistor #(.gate("br"), .width(8)) transistor_2 (
    .in(demultiplexer_1_out2), .out(transistor_2_out), .gate(not_2_out));
  Transistor #(.gate("br"), .width(8)) transistor_3 (
    .in(demultiplexer_1_out1), .out(transistor_3_out), .gate(not_4_out));
  Transistor #(.gate("br"), .width(8)) transistor_4 (
    .in(demultiplexer_1_out0), .out(transistor_4_out), .gate(not_5_out));
  Register R4 (.D(transistor_1_out), .en(1'b1), .Q(R4_q), .clk(T2_Clock), .clr(Reset_Registers));
  Register R3 (.D(transistor_2_out), .en(1'b1), .Q(R3_q), .clk(T2_Clock), .clr(Reset_Registers));
  Register R2 (.D(transistor_3_out), .en(1'b1), .Q(R2_q), .clk(T2_Clock), .clr(Reset_Registers));
  Register R1 (.D(transistor_4_out), .en(1'b1), .Q(R1_q), .clk(T2_Clock), .clr(Reset_Registers));
  Multiplexer #(.select(2), .width(8)) multiplexer_1 (
    .in0(R1_q), .in1(R2_q), .in2(R3_q), .in3(R4_q), .out(A_Data), .sel(A_Address), .en(1'b1));
  Multiplexer #(.select(2), .width(8)) multiplexer_2 (
    .in0(R1_q), .in1(R2_q), .in2(R3_q), .in3(R4_q), .out(B_Data), .sel(B_Address), .en(1'b1));
endmodule

module ALU (
  input  [7:0] RB,
  input  [7:0] RA,
  input  Carry_Bit_IN,
  input  Carry_Bit_IN_2,
  input  [2:0] ALU_OP_SELECT,
  output [7:0] _8_15_Bits,
  output Sign_Bit,
  output [7:0] _0_7_Bits,
  output Carry_Bit_OUT
);

  wire [7:0] adder_1_out, and_1_out, multiplier_1_cout, multiplier_1_out,
       n2_s_complement_alu_1_sub_modified_answer, or_1_out, subtractor_1_out, xor_1_out;

  Multiplier multiplier_1 (.a(RB), .b(RA), .out(multiplier_1_out), .cin({8{1'b0}}), .cout(multiplier_1_cout));
  Subtractor subtractor_1 (.a(RB), .b(RA), .out(subtractor_1_out), .bin(Carry_Bit_IN), .bout(Sign_Bit));
  Adder adder_1 (.a(RB), .b(RA), .out(adder_1_out), .cin(Carry_Bit_IN_2), .cout(Carry_Bit_OUT));
  assign and_1_out = RB & RA;  // AND_Gate and_1, 8 bits wide
  assign or_1_out = RB | RA;  // OR_Gate or_1, 8 bits wide
  assign xor_1_out = RB ^ RA;  // XOR_Gate xor_1, 8 bits wide
  _2_s_Complement_ALU u_2_s_complement_alu_1 (
    .SUB_Original_Ans(subtractor_1_out), .Sign_Bit(Sign_Bit),
    .SUB_Modified_Answer(n2_s_complement_alu_1_sub_modified_answer));
  Multiplexer #(.select(3), .width(8)) multiplexer_1 (
    .in0(multiplier_1_cout), .in1({8{1'b0}}), .in2({{7{1'b0}}, Carry_Bit_OUT}), .in3({8{1'b0}}),
    .in4({8{1'b0}}), .in5({8{1'b0}}), .in6({8{1'b0}}), .in7({8{1'b0}}), .out(_8_15_Bits),
    .sel(ALU_OP_SELECT), .en(1'b1));
  Multiplexer #(.select(3), .width(8)) multiplexer_2 (
    .in0(multiplier_1_out), .in1(n2_s_complement_alu_1_sub_modified_answer), .in2(adder_1_out),
    .in3(and_1_out), .in4(or_1_out), .in5(xor_1_out), .in6(RA), .out(_0_7_Bits), .sel(ALU_OP_SELECT),
    .en(1'b1));  // open: in7

  // Notes on the sheet:
  //   000- Multiply
  //   001- Subtract
  //   010- Addition
  //   011- AND OP
  //   100- OR OP
  //   101- XOR OP
  //   110- No Operation
endmodule

// Step_Counter
module Step_Counter (
  input  Main_Power_Step_counter,
  input  Main_Clock,
  output T8,
  output T1,
  output T2,
  output T3,
  output T4,
  output T5,
  output T6,
  output T7
);

  wire propogation_delay_1_out_2;
  wire [2:0] counter_1_q;

  Counter #(.width(3), .max('h7)) counter_1 (
    .load(1'b0), .D(3'b000), .count(1'b1), .Q(counter_1_q), .clk(Main_Clock), .clr(1'b0));  // open: carry
  Propogation_Delay propogation_delay_1 (.in_1(Main_Clock), .out_2(propogation_delay_1_out_2));
  Demultiplexer #(.select(3)) demultiplexer_1 (
    .out0(T8), .out1(T1), .out2(T2), .out3(T3), .out4(T4), .out5(T5), .out6(T6), .out7(T7),
    .in(propogation_delay_1_out_2), .sel(counter_1_q), .en(Main_Power_Step_counter));
endmodule

module Propogation_Delay (
  input  in_1,
  output out_2
);

  wire buffer_1_out, buffer_2_out, buffer_3_out, buffer_4_out, buffer_5_out, buffer_6_out, buffer_7_out,
       buffer_8_out, buffer_9_out;

  buf buffer_1 (buffer_1_out, buffer_3_out);
  buf buffer_2 (buffer_2_out, buffer_4_out);
  buf buffer_3 (buffer_3_out, in_1);
  buf buffer_4 (buffer_4_out, buffer_1_out);
  buf buffer_5 (buffer_5_out, buffer_2_out);
  buf buffer_6 (buffer_6_out, buffer_7_out);
  buf buffer_7 (buffer_7_out, buffer_8_out);
  buf buffer_8 (buffer_8_out, buffer_5_out);
  buf buffer_9 (buffer_9_out, buffer_6_out);
  buf buffer_10 (out_2, buffer_9_out);
endmodule

module _2_s_Complement_ALU (
  input  Sign_Bit,
  input  [7:0] SUB_Original_Ans,
  output [7:0] SUB_Modified_Answer
);

  wire [7:0] adder_1_out, demultiplexer_1_out0, demultiplexer_1_out1, not_1_out;

  Demultiplexer #(.width(8)) demultiplexer_1 (
    .out0(demultiplexer_1_out0), .out1(demultiplexer_1_out1), .in(SUB_Original_Ans), .sel(Sign_Bit), .en(1'b1));
  assign not_1_out = ~demultiplexer_1_out1;  // NOT_Gate not_1, 8 bits wide
  Adder adder_1 (.a(not_1_out), .b(8'h1), .out(adder_1_out));  // open: cin, cout
  Multiplexer #(.width(8)) multiplexer_1 (
    .in0(demultiplexer_1_out0), .in1(adder_1_out), .out(SUB_Modified_Answer), .sel(Sign_Bit), .en(1'b1));
endmodule

// IR_decoder
module Instruction_Register_And_Decoder (
  input  [7:0] MDR_to_IR_Data,
  input  IR_Clock,
  input  Reset_IR,
  output Mul_Enable,
  output Sub_Enable,
  output Add_Enable,
  output And_Enable,
  output Or_Enable,
  output XOR_Enable,
  output Move_Enable,
  output Load_Enable,
  output Store_Enable,
  output Jump_Enable,
  output Halt_Enable,
  output [1:0] B_Address,
  output [1:0] A_Address,
  output No_Operation_decoded_CSig_MDR,
  output [2:0] ALU_Opcode
);

  wire [3:0] register_1_q;

  Register register_1 (
    .D(MDR_to_IR_Data), .en(1'b1), .Q({B_Address, A_Address, register_1_q}), .clk(IR_Clock), .clr(Reset_IR));
  Demultiplexer #(.select(4)) demultiplexer_1 (
    .out0(Mul_Enable), .out1(Sub_Enable), .out2(Add_Enable), .out3(And_Enable), .out4(Or_Enable),
    .out5(XOR_Enable), .out6(Move_Enable), .out7(Load_Enable), .out8(Store_Enable), .out9(Jump_Enable),
    .out10(Halt_Enable), .in(1'b1), .sel(register_1_q), .en(1'b1));  // open: out11, out12, out13, out14, out15
  or or_1 (No_Operation_decoded_CSig_MDR, Move_Enable, Load_Enable, Store_Enable, Jump_Enable, Halt_Enable);
  Multiplexer #(.width(3)) multiplexer_1 (
    .in0(register_1_q[2:0]), .in1(3'b110), .out(ALU_Opcode), .sel(No_Operation_decoded_CSig_MDR), .en(1'b1));
endmodule

module Control_Unit (
  input  T1,
  input  T3,
  input  T2,
  input  T4,
  input  T5,
  input  T6,
  input  T7,
  input  T8,
  input  Load,
  input  Store,
  input  Jmp,
  output MAR_clock,
  output IR_Clock,
  output Memory_Select,
  output Load_2,
  output MDR_Clock,
  output PC_Clock,
  output RM_clock,
  output RY,
  output RF_Clock,
  output JMP_Enable
);

  wire and_3_out, and_4_out, and_5_out, and_6_out, and_7_out, counter_1_q, counter_2_q, counter_3_carry,
       not_1_out, not_2_out, not_4_out, not_5_out, not_6_out, not_7_out, not_8_out, not_9_out, not_10_out,
       or_2_out, or_3_out, or_4_out, or_5_out, or_7_out, or_10_out, or_11_out, transistor_2_out;

  not not_1 (not_1_out, T1);
  not not_2 (not_2_out, T3);
  not not_3 (Memory_Select, T2);
  not not_4 (not_4_out, T7);
  not not_5 (not_5_out, T8);
  not not_6 (not_6_out, T5);
  or or_1 (RF_Clock, T8, Jmp, Store);
  or or_2 (or_2_out, Load, Store);
  or or_3 (or_3_out, T2, T4);
  or or_4 (or_4_out, T2, T4);
  and and_1 (RM_clock, T5, Store);
  // AND_Gate and_2 has open pins: in0=T7, in1=Load, out=open
  and and_3 (and_3_out, T7, or_2_out);
  and and_4 (and_4_out, not_1_out, not_2_out);
  and and_5 (and_5_out, T6, or_2_out);
  or or_5 (or_5_out, T3, T1, T2, T4);
  or or_6 (MDR_Clock, or_3_out, and_3_out);
  not not_7 (not_7_out, and_4_out);
  and and_6 (and_6_out, T5, Jmp);
  or or_7 (or_7_out, T6, T7);
  not not_8 (not_8_out, Store);
  or or_8 (MAR_clock, not_7_out, and_5_out);
  Counter #(.width(1), .max('h1)) counter_1 (.Q(counter_1_q), .clk(or_5_out));  // open: load, D, count, carry, clr
  Transistor #(.gate("br")) transistor_1 (.in(Memory_Select), .out(Load_2), .gate(not_9_out));
  not not_9 (not_9_out, counter_1_q);
  or or_9 (PC_Clock, or_4_out, and_6_out);
  Counter #(.width(1), .max('h1)) counter_2 (.Q(counter_2_q), .clk(or_7_out));  // open: load, D, count, carry, clr
  or or_10 (or_10_out, T7, not_8_out);
  Transistor #(.gate("br")) transistor_2 (.in(or_10_out), .out(transistor_2_out), .gate(not_10_out));
  not not_10 (not_10_out, counter_2_q);
  or or_11 (or_11_out, T7, T3);
  and and_7 (and_7_out, Jmp, T7);
  Propogation_Delay propogation_delay_1 (.in_1(transistor_2_out), .out_2(Load_2));
  Counter #(.width(1), .max('h1)) counter_3 (
    .count(1'b1), .carry(counter_3_carry), .clk(or_11_out));  // open: load, D, Q, clr
  and and_8 (JMP_Enable, counter_3_carry, Jmp);

  assign IR_Clock = T3;
  assign RY = T5;
endmodule

module t1 (
  input  T1,
  output Mux_PC_Increment_Enable,
  output Mux_PC_Select_Enable,
  output MAR_Mux_Enable,
  output MAR_Mux_Select,
  output MAR_enable,
  output MAR_clock,
  output PC_Clock,
  output PC_Enable
);

  not not_1 (MAR_Mux_Enable, T1);

  assign MAR_clock = T1;
  assign MAR_enable = T1;
  assign MAR_Mux_Select = T1;
  assign Mux_PC_Increment_Enable = MAR_Mux_Enable;
  assign Mux_PC_Select_Enable = MAR_Mux_Enable;
  assign PC_Clock = T1;
  assign PC_Enable = T1;
endmodule

module t2 (
  input  T2,
  output Memory_Select,
  output Store0_Load1,
  output MDR_Clock,
  output MDR_Enable
);

  not not_1 (Memory_Select, T2);

  assign MDR_Clock = T2;
  assign MDR_Enable = T2;
  assign Store0_Load1 = Memory_Select;
endmodule

module T3 (
  input  T1,
  input  T2,
  input  T3,
  output MAR_Mux_Enable,
  output MAR_Mux_Select,
  output MAR_enable,
  output MAR_clock,
  output Memory_Select,
  output Store0_Load1,
  output MDR_Clock,
  output MDR_Enable,
  output MAR_Mux_Enable_2,
  output Store0_Load1_2,
  output IR_Clock,
  output IR_Enable,
  output MAR_Mux_Select_2,
  output MAR_enable_2,
  output MAR_clock_2
);

  not not_1 (MAR_Mux_Enable, T1);
  not not_2 (Memory_Select, T2);
  not not_3 (MAR_Mux_Enable_2, T3);

  assign IR_Clock = T3;
  assign IR_Enable = T3;
  assign MAR_clock = T1;
  assign MAR_clock_2 = T3;
  assign MAR_enable = T1;
  assign MAR_enable_2 = T3;
  assign MAR_Mux_Select = T1;
  assign MAR_Mux_Select_2 = T3;
  assign MDR_Clock = T2;
  assign MDR_Enable = T2;
  assign Store0_Load1 = Memory_Select;
  assign Store0_Load1_2 = T3;
endmodule

module Temp (
  input  [7:0] Jump_Offset,
  input  CC_Jump_Enable,
  input  T3,
  input  [7:0] Subroutine_Call_Address,
  input  Subroutine_Call_enable,
  input  Reset,
  input  Main_Clock,
  input  [7:0] Load_Store_Address_RY,
  input  Main_Power,
  input  Reset_MAR,
  input  Reset_Memory,
  input  [7:0] MDR_in,
  input  Reset_IR,
  input  Reset_MDR,
  input  T2_IR_DMux_Enable,
  output Carry,
  output Mul_Enable,
  output Sub_Enable,
  output Add_Enable,
  output And_Enable,
  output Or_Enable,
  output XOR_Enable,
  output Move_Enable,
  output Load_Enable,
  output Store_Enable,
  output Jump_Enable,
  output Halt_Enable
);

  wire not_1_out, not_2_out, step_counter_1_t2, step_counter_1_t3, step_counter_1_t4, step_counter_1_t5,
       undriven, undriven_2, undriven_3, undriven_4, undriven_5, undriven_6, undriven_7, undriven_8,
       undriven_9, undriven_10, undriven_12, undriven_13, undriven_15, undriven_16;
  wire [1:0] register_3_q_2, register_3_q_3;
  wire [3:0] register_3_q;
  wire [7:0] adder_1_out, MAR_q, MDR_q, multiplexer_1_out, multiplexer_2_out, multiplexer_3_out, PC_q,
       transistor_1_out, transistor_2_out, undriven_11, undriven_14;

  Multiplexer #(.width(8)) multiplexer_1 (
    .in0(PC_q), .in1(Load_Store_Address_RY), .out(multiplexer_1_out), .sel(undriven_8), .en(undriven_6));
  not not_1 (not_1_out, T3);
  Register MAR (.D(multiplexer_1_out), .en(undriven), .Q(MAR_q), .clk(undriven_9), .clr(Reset_MAR));
  Control_Unit control_unit_1 ();  // open: T1, T3, T2, T4, T5, T6, T7, T8, IR_Clock, Memory_Select, MDR_Clock, RY, PC_Clock, Load, Jmp, Store, RM_clock, MAR_clock, RF_Clock, Load_2, JMP_Enable
  Transistor #(.gate("br"), .width(8)) transistor_1 (.in(MDR_q), .out(transistor_1_out), .gate(undriven_12));
  RAM #(.bus("asynch")) ram_1 (
    .addr(MAR_q), .data(transistor_1_out), .sel(undriven_2), .ld(undriven_12), .clr(Reset_Memory));
  Transistor #(.gate("br"), .width(8)) transistor_2 (.in(transistor_1_out), .out(transistor_2_out), .gate(not_2_out));
  Transistor #(.width(8)) transistor_3 (.in(MDR_in), .out(transistor_2_out), .gate(undriven_12));
  not not_2 (not_2_out, undriven_12);
  Register MDR (.D(transistor_2_out), .en(undriven_13), .Q(MDR_q), .clk(undriven_3), .clr(Reset_MDR));
  Register register_1 (.D(undriven_11), .en(1'b1), .clk(step_counter_1_t5));  // open: Q, clr
  Step_Counter step_counter_1 (
    .Main_Clock(Main_Clock), .T2(step_counter_1_t2), .T3(step_counter_1_t3), .T4(step_counter_1_t4),
    .T5(step_counter_1_t5), .Main_Power_Step_counter(Main_Power));  // open: T8, T1, T6, T7
  Multiplexer #(.width(8)) multiplexer_2 (
    .in0(adder_1_out), .in1(Subroutine_Call_Address), .out(multiplexer_2_out), .sel(Subroutine_Call_enable),
    .en(undriven_7));
  Register PC (.D(multiplexer_2_out), .en(undriven_4), .Q(PC_q), .clk(undriven_15), .clr(Reset));
  Register register_2 (.D(undriven_14), .en(1'b1), .clk(step_counter_1_t5));  // open: Q, clr
  Multiplexer #(.width(8)) multiplexer_3 (
    .in0(8'h1), .in1(Jump_Offset), .out(multiplexer_3_out), .sel(CC_Jump_Enable), .en(undriven_5));
  Register register_3 (
    .D(MDR_q), .en(undriven_10), .Q({register_3_q_3, register_3_q_2, register_3_q}), .clk(undriven_16),
    .clr(Reset_IR));
  Adder adder_1 (.a(multiplexer_3_out), .b(PC_q), .out(adder_1_out), .cin(1'b0), .cout(Carry));
  Demultiplexer #(.select(4)) demultiplexer_1 (
    .out0(Mul_Enable), .out1(Sub_Enable), .out2(Add_Enable), .out3(And_Enable), .out4(Or_Enable),
    .out5(XOR_Enable), .out6(Move_Enable), .out7(Load_Enable), .out8(Store_Enable), .out9(Jump_Enable),
    .out10(Halt_Enable), .in(1'b1), .sel(register_3_q), .en(T2_IR_DMux_Enable));  // open: out11, out12, out13, out14, out15
endmodule

module CS_Control (
  input  T1,
  input  T2,
  input  T3,
  output MAR_Mux_Enable,
  output MAR_Mux_Select,
  output MAR_enable,
  output MAR_clock,
  output Memory_Select,
  output Store0_Load1,
  output MDR_Clock,
  output MDR_Enable,
  output MAR_Mux_Enable_2,
  output Store0_Load1_2,
  output IR_Clock,
  output IR_Enable,
  output MAR_Mux_Select_2,
  output MAR_enable_2,
  output MAR_clock_2,
  output Memory_Select_2
);

  wire counter_1_q, not_4_out, or_1_out;

  not not_1 (MAR_Mux_Enable, T1);
  not not_2 (Store0_Load1, T2);
  not not_3 (MAR_Mux_Enable_2, T3);
  or or_1 (or_1_out, T1, T2);
  Counter #(.width(1), .max('h1)) counter_1 (
    .count(1'b1), .Q(counter_1_q), .clk(or_1_out));  // open: load, D, carry, clr
  not not_4 (not_4_out, counter_1_q);
  Transistor transistor_1 (.in(Store0_Load1), .out(Memory_Select), .gate(not_4_out));

  assign IR_Clock = T3;
  assign IR_Enable = T3;
  assign MAR_clock = T1;
  assign MAR_clock_2 = T3;
  assign MAR_enable = T1;
  assign MAR_enable_2 = T3;
  assign MAR_Mux_Select = T1;
  assign MAR_Mux_Select_2 = T3;
  assign MDR_Clock = T2;
  assign MDR_Enable = T2;
  assign Store0_Load1_2 = T3;
endmodule

module PC (
  input  CC_Jump_Enable,
  input  [7:0] Subroutine_Call_Address,
  input  [7:0] Jump_Offset,
  input  Halt,
  input  Subroutine_Call_enable,
  input  PC_Clock,
  input  Reset,
  output [7:0] JMP
);

  wire [7:0] adder_1_out, multiplexer_1_out, multiplexer_2_out;

  Multiplexer #(.width(8)) multiplexer_1 (
    .in0(adder_1_out), .in1(Subroutine_Call_Address), .out(multiplexer_1_out), .sel(Subroutine_Call_enable),
    .en(1'b1));
  Register #(.trigger("falling")) PC (.D(multiplexer_1_out), .en(1'b1), .Q(JMP), .clk(PC_Clock), .clr(Reset));
  Adder adder_1 (.a(multiplexer_2_out), .b(JMP), .out(adder_1_out), .cin(1'b0));  // open: cout
  Multiplexer #(.select(2), .width(8)) multiplexer_2 (
    .in0(8'h1), .in1(Jump_Offset), .in2({8{1'b0}}), .out(multiplexer_2_out), .sel({Halt, CC_Jump_Enable}),
    .en(1'b1));  // open: in3
endmodule

module PD8 (
  input  [7:0] in_1,
  output [7:0] out_2
);

  wire [7:0] buffer_1_out, buffer_2_out, buffer_3_out, buffer_4_out, buffer_5_out, buffer_6_out,
       buffer_7_out, buffer_8_out, buffer_10_out;

  assign buffer_1_out = buffer_2_out;  // Buffer buffer_1, 8 bits wide
  assign buffer_2_out = in_1;  // Buffer buffer_2, 8 bits wide
  assign buffer_3_out = buffer_4_out;  // Buffer buffer_3, 8 bits wide
  assign buffer_4_out = buffer_1_out;  // Buffer buffer_4, 8 bits wide
  assign buffer_5_out = buffer_6_out;  // Buffer buffer_5, 8 bits wide
  assign buffer_6_out = buffer_8_out;  // Buffer buffer_6, 8 bits wide
  assign buffer_7_out = buffer_5_out;  // Buffer buffer_7, 8 bits wide
  assign buffer_8_out = buffer_3_out;  // Buffer buffer_8, 8 bits wide
  assign out_2 = buffer_10_out;  // Buffer buffer_9, 8 bits wide
  assign buffer_10_out = buffer_7_out;  // Buffer buffer_10, 8 bits wide
endmodule
